// Logisim project ALU.circ as structural Verilog: 2 circuits, main circuit main
module main (
  input  [2:0] ALUOp,
  input  [15:0] A,
  input  [15:0] B,
  input  in_4,
  output [15:0] Result,
  output [15:0] HI,
  output [15:0] LO,
  output GT,
  output Zero,
  output LT
);

  wire decoder_1_out4, decoder_1_out5, or_1_out;
  wire [15:0] adder_1_out, and_1_out, divider_1_out, divider_1_rem, multiplexer_1_out, multiplexer_2_out,
       multiplier_1_cout, multiplier_1_out, nor_1_out, shifter_1_out, shifter_2_out, subtractor_1_out,
       undriven;

  assign and_1_out = A & B & undriven;  // AND_Gate and_1, 16 bits wide
  assign nor_1_out = ~(undriven | A | B);  // NOR_Gate nor_1, 16 bits wide
  Adder #(.width(16)) adder_1 (.a(A), .b(B), .out(adder_1_out));  // open: cin, cout
  Subtractor #(.width(16)) subtractor_1 (.a(A), .b(B), .out(subtractor_1_out));  // open: bin, bout
  Multiplier #(.width(16)) multiplier_1 (.a(A), .b(B), .out(multiplier_1_out), .cout(multiplier_1_cout));  // open: cin
  Divider #(.width(16)) divider_1 (.a(A), .b(B), .out(divider_1_out), .rem(divider_1_rem));  // open: upper
  Decoder #(.select(3)) decoder_1 (
    .out4(decoder_1_out4), .out5(decoder_1_out5), .sel(ALUOp));  // open: out0, out1, out2, out3, out6, out7, en
  Comparator #(.width(16)) comparator_1 (.a(A), .b({16{1'b0}}), .gt(GT), .eq(Zero), .lt(LT));
  Multiplexer #(.width(16)) multiplexer_1 (
    .in0(multiplier_1_cout), .in1(divider_1_rem), .out(multiplexer_1_out), .sel(decoder_1_out5));  // open: en
  Multiplexer #(.width(16)) multiplexer_2 (
    .in0(multiplier_1_out), .in1(divider_1_out), .out(multiplexer_2_out), .sel(decoder_1_out5));  // open: en
  or or_1 (or_1_out, decoder_1_out4, decoder_1_out5);
  Shifter #(.width(16)) shifter_1 (.in(A), .\dist (B[3:0]), .out(shifter_1_out));
  Shifter #(.width(16), .shift("lr")) shifter_2 (.in(A), .\dist (B[3:0]), .out(shifter_2_out));
  Register #(.width(16)) u_HI (.D(multiplexer_1_out), .en(or_1_out), .Q(HI), .clk(in_4));  // open: clr
  Register #(.width(16)) u_LO (.D(multiplexer_2_out), .en(or_1_out), .Q(LO), .clk(in_4));  // open: clr
  Multiplexer #(.select(3), .width(16)) multiplexer_3 (
    .in0(and_1_out), .in1(nor_1_out), .in2(adder_1_out), .in3(subtractor_1_out), .in4({16{1'b0}}),
    .in5({16{1'b0}}), .in6(shifter_1_out), .in7(shifter_2_out), .out(Result), .sel(ALUOp));  // open: en

  // Other names for the same wires on the sheet: Clock = in_4

  // Notes on the sheet:
  //   Inputs
  //   Shane Riley - spr33
  //   Outputs
  //   Design your ALU in this file
  //   A - First ALU input
  //   B - Second ALU input
  //   Result - ALU main result
  //   HI/LO the value of the ALU registers using for mul/div
  //   GT/Zero/LT - Comparison of input A with zero
  //   ALUOp - The control signal defining the behaviour of the ALU
endmodule

module test (
  input  [2:0] in_1,
  input  [15:0] in_2,
  input  [15:0] in_3
);

  wire button_1_out, main_1_gt, main_1_lt, main_1_zero;
  wire [15:0] main_1_hi, main_1_lo, main_1_result;

  main main_1 (
    .ALUOp(in_1), .A(in_2), .B(in_3), .Result(main_1_result), .GT(main_1_gt), .Zero(main_1_zero),
    .LT(main_1_lt), .in_4(button_1_out), .HI(main_1_hi), .LO(main_1_lo));
  Button button_1 (.out(button_1_out));
  // Probe on main_1_result
  // Probe on main_1_hi
  // Probe on main_1_lo
  // Probe on main_1_gt
  // Probe on main_1_zero
  // Probe on main_1_lt

  // Notes on the sheet:
  //   Test your circuit!
endmodule
