// Logisim project RegFile.circ as structural Verilog: 2 circuits, main circuit main
module main (
  input  [15:0] WriteData0,
  input  [2:0] WriteSelect0,
  input  [2:0] ReadSelect0,
  input  [2:0] ReadSelect1,
  input  WE0,
  input  Clock,
  output [15:0] Reg0,
  output [15:0] Reg1,
  output [15:0] Reg2,
  output [15:0] Reg3,
  output [15:0] Reg4,
  output [15:0] Reg5,
  output [15:0] Reg6,
  output [15:0] Reg7,
  output [15:0] ReadData0,
  output [15:0] ReadData1
);

  wire decoder_1_out0, decoder_1_out1, decoder_1_out2, decoder_1_out3, decoder_1_out4, decoder_1_out5,
       decoder_1_out6, decoder_1_out7;
  wire [15:0] controlled_buffer_1_out, controlled_buffer_2_out, controlled_buffer_3_out,
       controlled_buffer_4_out, controlled_buffer_5_out, controlled_buffer_6_out, controlled_buffer_7_out,
       controlled_buffer_8_out;

  Decoder #(.select(3)) decoder_1 (
    .out0(decoder_1_out0), .out1(decoder_1_out1), .out2(decoder_1_out2), .out3(decoder_1_out3),
    .out4(decoder_1_out4), .out5(decoder_1_out5), .out6(decoder_1_out6), .out7(decoder_1_out7),
    .sel(WriteSelect0));  // open: en
  assign controlled_buffer_1_out = decoder_1_out0 ? WriteData0 : 16'bz;  // Controlled_Buffer controlled_buffer_1
  assign controlled_buffer_2_out = decoder_1_out1 ? WriteData0 : 16'bz;  // Controlled_Buffer controlled_buffer_2
  assign controlled_buffer_3_out = decoder_1_out2 ? WriteData0 : 16'bz;  // Controlled_Buffer controlled_buffer_3
  assign controlled_buffer_4_out = decoder_1_out3 ? WriteData0 : 16'bz;  // Controlled_Buffer controlled_buffer_4
  assign controlled_buffer_5_out = decoder_1_out4 ? WriteData0 : 16'bz;  // Controlled_Buffer controlled_buffer_5
  assign controlled_buffer_6_out = decoder_1_out5 ? WriteData0 : 16'bz;  // Controlled_Buffer controlled_buffer_6
  assign controlled_buffer_7_out = decoder_1_out6 ? WriteData0 : 16'bz;  // Controlled_Buffer controlled_buffer_7
  assign controlled_buffer_8_out = decoder_1_out7 ? WriteData0 : 16'bz;  // Controlled_Buffer controlled_buffer_8
  Register #(.width(16)) register_1 (.D(controlled_buffer_1_out), .en(WE0), .Q(Reg0), .clk(Clock));  // open: clr
  Register #(.width(16)) register_2 (.D(controlled_buffer_2_out), .en(WE0), .Q(Reg1), .clk(Clock));  // open: clr
  Register #(.width(16)) register_3 (.D(controlled_buffer_3_out), .en(WE0), .Q(Reg2), .clk(Clock));  // open: clr
  Register #(.width(16)) register_4 (.D(controlled_buffer_4_out), .en(WE0), .Q(Reg3), .clk(Clock));  // open: clr
  Register #(.width(16)) register_5 (.D(controlled_buffer_5_out), .en(WE0), .Q(Reg4), .clk(Clock));  // open: clr
  Register #(.width(16)) register_6 (.D(controlled_buffer_6_out), .en(WE0), .Q(Reg5), .clk(Clock));  // open: clr
  Register #(.width(16)) register_7 (.D(controlled_buffer_7_out), .en(WE0), .Q(Reg6), .clk(Clock));  // open: clr
  Register #(.width(16)) register_8 (.D(controlled_buffer_8_out), .en(WE0), .Q(Reg7), .clk(Clock));  // open: clr
  Multiplexer #(.select(3), .width(16)) multiplexer_1 (
    .in0(Reg0), .in1(Reg1), .in2(Reg2), .in3(Reg3), .in4(Reg4), .in5(Reg5), .in6(Reg6), .in7(Reg7),
    .out(ReadData0), .sel(ReadSelect0));  // open: en
  Multiplexer #(.select(3), .width(16)) multiplexer_2 (
    .in0(Reg0), .in1(Reg1), .in2(Reg2), .in3(Reg3), .in4(Reg4), .in5(Reg5), .in6(Reg6), .in7(Reg7),
    .out(ReadData1), .sel(ReadSelect1));  // open: en

  // Other names for the same wires on the sheet: WriteEnable0 = WE0

  // Notes on the sheet:
  //   Inputs
  //   Shane Riley - spr33
  //   Add the registers to this file
  //   WriteSelect0 - Register to write to
  //   WE0 - Enable writing to 1 register
  //   ReadSelect0 - First register to read data from
  //   ReadSelect1 - Second register to read data from
  //   ReadData0 - Data being read from first register
  //   ReadData1 - Data being read from second register
  //   WriteData0 - The data to be written to register by most instructions
  //   and design the logic to control them
endmodule

module test (
  input  [15:0] Write_data_A,
  input  Write_Enable_Port_A,
  input  [2:0] in_3,
  input  [2:0] Select_Read_A,
  input  [2:0] Select_Read_B
);

  wire Clock_out;
  wire [15:0] main_1_readdata0, main_1_readdata1, main_1_reg0, main_1_reg1, main_1_reg2, main_1_reg3,
       main_1_reg4, main_1_reg5, main_1_reg6, main_1_reg7;

  // Probe on main_1_reg0
  // Probe on main_1_reg1
  // Probe on main_1_reg3
  // Probe on main_1_reg2
  Button Clock (.out(Clock_out));
  // Probe on main_1_reg5
  // Probe on main_1_reg4
  // Probe on main_1_reg6
  // Probe on main_1_reg7
  main main_1 (
    .ReadData0(main_1_readdata0), .ReadData1(main_1_readdata1), .Reg0(main_1_reg0), .Reg1(main_1_reg1),
    .Reg2(main_1_reg2), .Reg3(main_1_reg3), .Reg4(main_1_reg4), .Reg5(main_1_reg5), .Reg6(main_1_reg6),
    .Reg7(main_1_reg7), .WriteData0(Write_data_A), .WriteSelect0(in_3), .ReadSelect0(Select_Read_A),
    .ReadSelect1(Select_Read_B), .WE0(Write_Enable_Port_A), .Clock(Clock_out));
  // Probe on main_1_readdata0
  // Probe on main_1_readdata1

  // Notes on the sheet:
  //   Test your circuit!
endmodule
