// Logisim project lab10B.circ as structural Verilog: 1 circuit, main circuit main
module main (
  input  WriteEnable,
  input  [1:0] ReadRegister1,
  input  [1:0] ReadRegister2,
  input  [1:0] WriteRegister,
  input  [15:0] WriteData,
  input  Clock,
  output [15:0] ReadData1,
  output [15:0] ReadData2
);

  wire decoder_1_out0, decoder_1_out1, decoder_1_out2, decoder_1_out3;
  wire [1:0] multiplexer_1_out;
  wire [15:0] multiplexer_2_out, multiplexer_3_out, multiplexer_4_out, multiplexer_5_out, register_1_q,
       register_2_q, register_3_q, register_4_q;

  Decoder #(.select(2)) decoder_1 (
    .out0(decoder_1_out0), .out1(decoder_1_out1), .out2(decoder_1_out2), .out3(decoder_1_out3),
    .sel(multiplexer_1_out));  // open: en
  Multiplexer #(.width(2)) multiplexer_1 (
    .in1(WriteRegister), .out(multiplexer_1_out), .sel(WriteEnable));  // open: in0, en
  Multiplexer #(.width(16)) multiplexer_2 (
    .in1(WriteData), .out(multiplexer_2_out), .sel(decoder_1_out0));  // open: in0, en
  Register #(.width(16)) register_1 (.D(multiplexer_2_out), .Q(register_1_q), .clk(Clock));  // open: en, clr
  Register #(.width(16)) register_2 (.D(multiplexer_3_out), .Q(register_2_q), .clk(Clock));  // open: en, clr
  Multiplexer #(.width(16)) multiplexer_3 (
    .in1(WriteData), .out(multiplexer_3_out), .sel(decoder_1_out1));  // open: in0, en
  Multiplexer #(.width(16)) multiplexer_4 (
    .in1(WriteData), .out(multiplexer_4_out), .sel(decoder_1_out2));  // open: in0, en
  Register #(.width(16)) register_3 (.D(multiplexer_4_out), .Q(register_3_q), .clk(Clock));  // open: en, clr
  Multiplexer #(.width(16)) multiplexer_5 (
    .in1(WriteData), .out(multiplexer_5_out), .sel(decoder_1_out3));  // open: in0, en
  Register #(.width(16)) register_4 (.D(multiplexer_5_out), .Q(register_4_q), .clk(Clock));  // open: en, clr
  Multiplexer #(.select(2), .width(16)) multiplexer_6 (
    .in0(register_1_q), .in1(register_2_q), .in2(register_3_q), .in3(register_4_q), .out(ReadData1),
    .sel(ReadRegister1));  // open: en
  Multiplexer #(.select(2), .width(16)) multiplexer_7 (
    .in0(register_1_q), .in1(register_2_q), .in2(register_3_q), .in3(register_4_q), .out(ReadData2),
    .sel(ReadRegister2));  // open: en

  // Notes on the sheet:
  //   of your circuit.
  //   These are the inputs
  //   Do not modify this!
  //   Put your name and id here: Shane Riley - spr33
  //   These are the outputs
  //   of your circuit.
  //   Do not modify this!
endmodule
