// Logisim project lab11A.circ as structural Verilog: 4 circuits, main circuit main
module main (
  output [15:0] Instruction,
  output [7:0] Immediate,
  output Register,
  output [3:0] Opcode,
  output [7:0] RegisterWriteData,
  output [7:0] Register0,
  output [7:0] Register1,
  output [7:0] ALUResult
);

  wire clock_1_out, dec_1_select, not_1_out;
  wire [1:0] dec_1_aluop;
  wire [7:0] adder_1_out, register_1_q;

  Adder adder_1 (.a(8'h1), .b(register_1_q), .out(adder_1_out));  // open: cin, cout
  Register register_1 (.D(adder_1_out), .en(1'b1), .Q(register_1_q), .clk(clock_1_out));  // open: clr
  Clock clock_1 (.out(clock_1_out));
  ROM #(.dataWidth(16)) rom_1 (.addr(register_1_q), .data(Instruction), .sel(1'b1));
  Fields fields_1 (.Instruction(Instruction), .Immediate(Immediate), .Register(Register), .Opcode(Opcode));
  Dec dec_1 (.Opcode(Opcode), .Select(dec_1_select), .ALUOp(dec_1_aluop));
  not not_1 (not_1_out, Register);
  Register register_2 (.D(RegisterWriteData), .en(not_1_out), .Q(Register0), .clk(clock_1_out));  // open: clr
  Register register_3 (.D(RegisterWriteData), .en(Register), .Q(Register1), .clk(clock_1_out));  // open: clr
  ALU alu_1 (.A(Register0), .B(Register1), .Operation(dec_1_aluop), .Result(ALUResult));
  Multiplexer #(.width(8)) multiplexer_1 (
    .in0(ALUResult), .in1(Immediate), .out(RegisterWriteData), .sel(dec_1_select));  // open: en
endmodule

module Fields (
  input  [15:0] Instruction,
  output [7:0] Immediate,
  output Register,
  output [3:0] Opcode
);


  assign Immediate = Instruction[7:0];
  assign Opcode = Instruction[15:12];
  assign Register = Instruction[11];
endmodule

module Dec (
  input  [3:0] Opcode,
  output Select,
  output [1:0] ALUOp
);

  wire decoder_1_out4, decoder_1_out5, decoder_1_out8, decoder_1_out9;

  Decoder #(.select(4)) decoder_1 (
    .out0(Select), .out4(decoder_1_out4), .out5(decoder_1_out5), .out8(decoder_1_out8),
    .out9(decoder_1_out9), .sel(Opcode));  // open: out1, out2, out3, out6, out7, out10, out11, out12, out13, out14, out15, en
  Priority_Encoder #(.select(2)) priority_encoder_1 (
    .in0(1'b1), .in1(decoder_1_out5), .in2(decoder_1_out9), .in3(decoder_1_out8), .out(ALUOp));  // open: gs, en_out, en_in
endmodule

module ALU (
  input  [7:0] A,
  input  [7:0] B,
  input  [1:0] Operation,
  output [7:0] Result
);

  wire [7:0] adder_1_out, nand_1_out, nor_1_out, subtractor_1_out, undriven;

  Adder adder_1 (.a(A), .b(B), .out(adder_1_out));  // open: cin, cout
  Subtractor subtractor_1 (.a(A), .b(B), .out(subtractor_1_out));  // open: bin, bout
  assign nand_1_out = ~(A & B & undriven);  // NAND_Gate nand_1, 8 bits wide
  assign nor_1_out = ~(undriven | A | B);  // NOR_Gate nor_1, 8 bits wide
  Multiplexer #(.select(2), .width(8)) multiplexer_1 (
    .in0(adder_1_out), .in1(subtractor_1_out), .in2(nand_1_out), .in3(nor_1_out), .out(Result),
    .sel(Operation));  // open: en
endmodule
