// Logisim project lab11B.circ as structural Verilog: 1 circuit, main circuit main
module main (
  input  clear,
  output sel,
  output ld,
  output [3:0] address,
  output [3:0] data
);

  wire and_1_p2, and_1_p3, counter_1_carry;
  wire [3:0] counter_1_q, counter_3_q;

  Counter #(.width(4), .max('hf), .ongoal("stay")) counter_1 (
    .Q(counter_1_q), .carry(counter_1_carry), .clk(and_1_p3), .clr(clear));  // open: load, D, count
  assign address = sel ? counter_1_q : 4'bz;  // Controlled_Buffer controlled_buffer_1
  Counter #(.width(2), .max('h2), .ongoal("stay")) counter_2 (
    .carry(ld), .clk(and_1_p2), .clr(clear));  // open: load, D, count, Q
  // AND_Gate and_1: pin names not known; wires that end beside it: counter_1_carry, and_1_p2, and_1_p3
  Clock clock_1 (.out(and_1_p3));
  RAM #(.addrWidth(4), .dataWidth(4)) ram_1 (
    .addr(address), .data(data), .sel(sel), .clk(and_1_p3), .ld(ld), .clr(clear));
  // NOT_Gate not_1: pin names not known; wires that end beside it: ld, sel
  assign data = sel ? counter_3_q : 4'bz;  // Controlled_Buffer controlled_buffer_2
  Counter #(.width(4), .max('hf), .ongoal("stay")) counter_3 (
    .Q(counter_3_q), .clk(and_1_p3), .clr(clear));  // open: load, D, count, carry

  // Other names for the same wires on the sheet: clr = clear

  // Notes on the sheet:
  //   These are the inputs
  //   of your circuit.
  //   Do not modify this!
  //   Put your name and id here: Shane Riley - spr33
  //   These are the outputs
  //   of your circuit.
  //   Do not modify this!
endmodule
