// Logisim project lab12C.circ as structural Verilog: 3 circuits, main circuit main
module main (
  input  Bit,
  input  Clock,
  output Output
);

  wire [1:0] getnextstate_1_newstate_0, register_1_q;

  Register #(.width(2)) register_1 (.D(getnextstate_1_newstate_0), .Q(register_1_q), .clk(Clock));  // open: en, clr
  getNextState getnextstate_1 (
    .State_1(register_1_q[1]), .State_0(register_1_q[0]), .Input(Bit),
    .NewState_1(getnextstate_1_newstate_0[1]), .NewState_0(getnextstate_1_newstate_0[0]));
  getOutput getoutput_1 (.State_1(register_1_q[1]), .State_0(register_1_q[0]), .Output(Output));

  // Notes on the sheet:
  //   of your circuit.
  //   These are the inputs
  //   Do not modify this!
  //   Shane Riley -- spr33
  //   These are the outputs
  //   of your circuit.
  //   Do not modify this!
endmodule

// Out
module getOutput (
  input  State_1,
  input  State_0,
  output Output
);

  and and_1 (Output, State_1, State_0);
endmodule

module getNextState (
  input  State_1,
  input  State_0,
  input  Input,
  output NewState_1,
  output NewState_0
);

  wire and_1_out, and_2_out, and_3_out, and_4_out, and_5_out, not_1_p2, not_2_p3, not_3_p4, not_4_p3,
       not_5_p3, not_6_p3;

  // NOT_Gate not_1: pin names not known; wires that end beside it: State_1, not_1_p2
  // NOT_Gate not_2: pin names not known; wires that end beside it: State_0, State_1, not_2_p3
  // NOT_Gate not_3: pin names not known; wires that end beside it: State_0, State_1, State_0, not_3_p4
  // NOT_Gate not_4: pin names not known; wires that end beside it: State_1, State_0, not_4_p3
  // NOT_Gate not_5: pin names not known; wires that end beside it: State_0, Input, not_5_p3
  // NOT_Gate not_6: pin names not known; wires that end beside it: State_0, Input, not_6_p3
  and and_1 (and_1_out, not_1_p2, State_0, Input);
  and and_2 (and_2_out, State_1, not_2_p3);
  and and_3 (and_3_out, not_3_p4, not_4_p3, Input);
  and and_4 (and_4_out, State_1, not_5_p3, not_6_p3);
  and and_5 (and_5_out, State_1, State_0, Input);
  // OR_Gate or_1: pin names not known; wires that end beside it: and_1_out, and_1_out, and_2_out, NewState_1
  or or_2 (NewState_0, and_3_out, and_4_out, and_5_out);
endmodule
