// Logisim project lab8B.circ as structural Verilog: 1 circuit, main circuit main
module main (
  input  A,
  input  B,
  input  C,
  output Q
);

  wire A1_out;

  and A1 (A1_out, B, C);
  or O1 (Q, A, A1_out);

  // Notes on the sheet:
  //   of your circuit.
  //   These are the inputs
  //   Do not modify this!
  //   Put your name and id here: Shane Riley - spr33
  //   These are the outputs
  //   of your circuit.
  //   Do not modify this!
endmodule
