// Logisim project lab8A.circ as structural Verilog: 1 circuit, main circuit main
module main (
  input  A,
  input  B,
  input  C_in,
  output S,
  output C_out
);

  wire and_1_out;

  and and_1 (and_1_out, A, B);
  or or_1 (C_out, and_1_out, C_in);

  assign S = C_out;

  // Notes on the sheet:
  //   These are the inputs
  //   of your circuit.
  //   Do not modify this!
  //   Put your name and id here: Luis Oliveira - lun8
  //   This circuit is wrong :D
  //   Implement here your adder!
  //   These are the outputs
  //   of your circuit.
  //   Do not modify this!
endmodule
