// Logisim project umips.circ as structural Verilog: 6 circuits, main circuit main
module main (
  output [15:0] Reg0,
  output [15:0] Reg1,
  output [15:0] Reg2,
  output [15:0] Reg3,
  output [15:0] Reg4,
  output [15:0] Reg5,
  output [15:0] Reg6,
  output [15:0] Reg7,
  output [3:0] Output3,
  output [3:0] Output2,
  output [3:0] Output1,
  output [3:0] Output0,
  output halt
);

  wire aluImm, clk, doHalt, doJumpToImm, doJumpToRs, doPut, doSignExtend, doWMem, doWReg, gt, isOn, lt,
       subOp, z;
  wire [2:0] ALUop, ARegAdd, BRegAdd;
  wire [3:0] opCode;
  wire [7:0] _8imm, adder_1_out, multiplexer_1_out, PC, PC_prime;
  wire [15:0] _16imm, aluA, aluB, aluRes, BRegData, HIReg, instruction, LOReg, Output, rMemData, wRegData;

  Clock clock_1 (.out(clk));
  LED led_1 (.in(halt));
  T_Flip_Flop t_ff_1 (.clk(clk), .T(doHalt), .Q(halt), .Qn(isOn));  // open: preset, reset, en
  Adder adder_1 (.a(PC), .b(8'h1), .out(adder_1_out));  // open: cin, cout
  Hex_Digit_Display hex_digit_display_1 (.value(Output2));  // open: dp
  Hex_Digit_Display hex_digit_display_2 (.value(Output3));  // open: dp
  Register #(.width(16)) Display (.D(Output), .Q({Output3, Output2, Output1, Output0}), .clk(clk));  // open: en, clr
  Multiplexer #(.width(8)) multiplexer_1 (
    .in0(adder_1_out), .in1(_8imm), .out(multiplexer_1_out), .sel(doJumpToImm));  // open: en
  Hex_Digit_Display hex_digit_display_3 (.value(Output1));  // open: dp
  Register register_1 (.D(PC_prime), .Q(PC), .clk(clk));  // open: en, clr
  Multiplexer #(.width(8)) multiplexer_2 (
    .in0(multiplexer_1_out), .in1(aluA[7:0]), .out(PC_prime), .sel(doJumpToRs));  // open: en
  Hex_Digit_Display hex_digit_display_4 (.value(Output0));  // open: dp
  assign Output = doPut ? aluA : 16'bz;  // Controlled_Buffer controlled_buffer_1
  signExtension signextension_1 (.Immediate(_8imm), .signExtend(doSignExtend), .Extended_Immediate(_16imm));
  ROM #(.dataWidth(16)) rom_1 (.addr(PC), .data(instruction), .sel(isOn));
  RegFile_main main_1 (
    .ReadData0(aluA), .ReadData1(BRegData), .Reg0(Reg0), .Reg1(Reg1), .Reg2(Reg2), .Reg3(Reg3), .Reg4(Reg4),
    .Reg5(Reg5), .Reg6(Reg6), .Reg7(Reg7), .WriteData0(wRegData), .WriteSelect0(ARegAdd),
    .ReadSelect0(ARegAdd), .ReadSelect1(BRegAdd), .WE0(doWReg), .Clock(clk));
  ALUController alucontroller_1 (.opCode(opCode), .subOp(subOp), .ALUop(ALUop));
  ALU_main main_2 (
    .ALUOp(ALUop), .A(aluA), .B(aluB), .Result(aluRes), .GT(gt), .Zero(z), .LT(lt), .in_4(clk), .HI(HIReg),
    .LO(LOReg));
  Multiplexer #(.width(16)) multiplexer_3 (.in0(BRegData), .in1(_16imm), .out(aluB), .sel(aluImm));  // open: en
  Fields fields_1 (
    .Instruction(instruction), .rs(ARegAdd), .rt(BRegAdd), .subOp(subOp), .opCode(opCode), ._8imm(_8imm),
    .iType(aluImm));
  Controller controller_1 (
    .gt(gt), .z(z), .lt(lt), .subOp(subOp), .opCode(opCode), .doHalt(doHalt), .doSignExtend(doSignExtend),
    .doPut(doPut), .doWMem(doWMem), .doWReg(doWReg), .doJumpToImm(doJumpToImm), .doJumpToRs(doJumpToRs));
  RAM #(.dataWidth(16), .bus("separate")) ram_1 (
    .addr(BRegData[7:0]), .din(aluA), .data(rMemData), .str(doWMem), .sel(isOn), .clk(clk));  // open: ld, clr
  REGIO regio_1 (
    .PC(PC), .rMemData(rMemData), .aluRes(aluRes), .HIReg(HIReg), .LOReg(LOReg), ._16imm(_16imm),
    .subOp(subOp), .opCode(opCode), .wRegData(wRegData));

  // Other names for the same wires on the sheet: memAdd[7:0] = BRegData[7:0]; rt[2:0] = BRegAdd;
  //   ARegData[15:0] = aluA; wMemData[15:0] = aluA; rs[2:0] = ARegAdd; wRegAdd[2:0] = ARegAdd

  // Notes on the sheet:
  //   Clock
  //   Halt
  //   nextLine
  //   PC
  //   SignExtension
  //   Put
  //   ROM
  //   Shane Riley uMips
  //   spr33
  //   contents of rom_1 (hex, n*v repeats v):
  //   1a06 2fdd 8e01 8a01 9000
  //   Regs
  //   You must connect Reg0..7 to the top ports of the register file.
  //   Reg
  //   ALUController
  //   ALUA
  //   ALUB
  //   Fields
  //   Connect Output3..0 to your LED display.
  //   Output3 is the most significant
  //   Controller
  //   RAM
  //   REG I/O
  //   :(
endmodule

// SE
module signExtension (
  input  signExtend,
  input  [7:0] Immediate,
  output [15:0] Extended_Immediate
);

  wire [15:0] bit_extender_1_out, bit_extender_2_out;

  assign bit_extender_1_out = {{8{1'b0}}, Immediate};  // Bit_Extender bit_extender_1
  assign bit_extender_2_out = {{8{Immediate[7]}}, Immediate};  // Bit_Extender bit_extender_2
  Multiplexer #(.width(16)) multiplexer_1 (
    .in0(bit_extender_1_out), .in1(bit_extender_2_out), .out(Extended_Immediate), .sel(signExtend));  // open: en
endmodule

// ALUC
module ALUController (
  input  [3:0] opCode,
  input  subOp,
  output [2:0] ALUop
);

  wire add_p3, and_out, decoder_1_out11, decoder_1_out12, decoder_1_out13, decoder_1_out14, decoder_1_out15,
       div_out, mul_out, nor_out, not_1_out, or_1_out, priority_encoder_1_en_out, sllv_out, srlv_out, sub_p4,
       sub_p5, undriven, undriven_2, undriven_3, undriven_4;
  wire [2:0] priority_encoder_1_out;

  Decoder #(.select(4)) decoder_1 (
    .out11(decoder_1_out11), .out12(decoder_1_out12), .out13(decoder_1_out13), .out14(decoder_1_out14),
    .out15(decoder_1_out15), .sel(opCode));  // open: out0, out1, out2, out3, out4, out5, out6, out7, out8, out9, out10, en
  not not_1 (not_1_out, subOp);
  and \and  (and_out, not_1_out, decoder_1_out14, undriven);
  and \nor  (nor_out, undriven, subOp, decoder_1_out14);
  // AND_Gate add: pin names not known; wires that end beside it: not_1_out, decoder_1_out15, add_p3
  or or_1 (or_1_out, nor_out, add_p3, decoder_1_out13);
  // AND_Gate sub: pin names not known; wires that end beside it: not_1_out, subOp, decoder_1_out15, sub_p4, sub_p5
  and mul (mul_out, sub_p4, subOp, decoder_1_out12, undriven_2);
  and div (div_out, undriven_2, not_1_out, decoder_1_out12, undriven_3);
  and sllv (sllv_out, undriven_3, subOp, decoder_1_out11, undriven_4);
  and srlv (srlv_out, undriven_4, not_1_out, decoder_1_out11);
  Priority_Encoder priority_encoder_1 (
    .in0(and_out), .in1(nor_out), .in2(or_1_out), .in3(sub_p5), .in4(mul_out), .in5(div_out), .in6(sllv_out),
    .in7(srlv_out), .out(priority_encoder_1_out), .en_out(priority_encoder_1_en_out));  // open: en_in, gs
  Multiplexer #(.width(3)) multiplexer_1 (
    .in0(priority_encoder_1_out), .in1(3'b000), .out(ALUop), .sel(priority_encoder_1_en_out));  // open: en

  // Notes on the sheet:
  //   ALUController
endmodule

module Fields (
  input  [15:0] Instruction,
  output [2:0] rs,
  output [2:0] rt,
  output subOp,
  output [3:0] opCode,
  output [7:0] _8imm,
  output iType
);

  wire and_1_p3, decoder_1_out1, decoder_1_out2, decoder_1_out4, decoder_1_out5, decoder_1_out6,
       decoder_1_out7, decoder_1_out13, not_1_p2;

  // NOT_Gate not_1: pin names not known; wires that end beside it: Instruction[0], not_1_p2
  Decoder #(.select(4)) decoder_1 (
    .out1(decoder_1_out1), .out2(decoder_1_out2), .out4(decoder_1_out4), .out5(decoder_1_out5),
    .out6(decoder_1_out6), .out7(decoder_1_out7), .out13(decoder_1_out13), .sel(Instruction[15:12]));  // open: out0, out3, out8, out9, out10, out11, out12, out14, out15, en
  // AND_Gate and_1: pin names not known; wires that end beside it: not_1_p2, decoder_1_out1, and_1_p3
  or or_1 (iType, and_1_p3, decoder_1_out2, decoder_1_out4, decoder_1_out5, decoder_1_out6, decoder_1_out7, decoder_1_out13);

  assign _8imm = Instruction[8:1];
  assign opCode = Instruction[15:12];
  assign rs = Instruction[11:9];
  assign rt = Instruction[8:6];
  assign subOp = Instruction[0];
endmodule

module Controller (
  input  gt,
  input  z,
  input  lt,
  input  subOp,
  input  [3:0] opCode,
  output doHalt,
  output doSignExtend,
  output doPut,
  output doWMem,
  output doWReg,
  output doJumpToImm,
  output doJumpToRs
);

  wire and_1_out, and_2_out, and_3_p4, and_7_out, and_8_out, and_9_out, and_10_out, and_11_out,
       decoder_1_out0, decoder_1_out1, decoder_1_out2, decoder_1_out10, decoder_1_out11, decoder_1_out13,
       decoder_1_out14, decoder_1_out15, decoder_2_out0, decoder_2_out1, decoder_2_out2, decoder_2_out13,
       decoder_3_out4, decoder_3_out5, decoder_3_out6, decoder_3_out7, not_1_out, not_2_out, not_3_out,
       or_2_p3, or_4_out, undriven, undriven_2, undriven_3;

  Decoder #(.select(4)) decoder_1 (
    .out0(decoder_1_out0), .out1(decoder_1_out1), .out2(decoder_1_out2), .out10(decoder_1_out10),
    .out11(decoder_1_out11), .out13(decoder_1_out13), .out14(decoder_1_out14), .out15(decoder_1_out15),
    .sel(opCode));  // open: out3, out4, out5, out6, out7, out8, out9, out12, en
  not not_1 (not_1_out, subOp);
  and and_1 (and_1_out, decoder_1_out0, subOp, undriven);
  and and_2 (and_2_out, undriven, decoder_1_out2, subOp, decoder_1_out1);
  // AND_Gate and_3: pin names not known; wires that end beside it: subOp, decoder_1_out1, not_1_out, and_3_p4
  Decoder #(.select(4)) decoder_2 (
    .out0(decoder_2_out0), .out1(decoder_2_out1), .out2(decoder_2_out2), .out8(doPut), .out9(doHalt),
    .out13(decoder_2_out13), .sel(opCode));  // open: out3, out4, out5, out6, out7, out10, out11, out12, out14, out15, en
  or or_1 (doWReg, and_1_out, and_2_out, and_3_p4, decoder_1_out10, decoder_1_out11, decoder_1_out13, decoder_1_out14, decoder_1_out15);
  not not_2 (not_2_out, subOp);
  // OR_Gate or_2: pin names not known; wires that end beside it: decoder_2_out2, decoder_2_out1, or_2_p3
  and and_4 (doJumpToRs, not_2_out, decoder_2_out0, decoder_2_out1);
  and and_5 (doWMem, decoder_2_out0, decoder_2_out1, subOp);
  and and_6 (doSignExtend, subOp, decoder_2_out13);
  and and_7 (and_7_out, not_2_out, or_2_p3);
  Decoder #(.select(4)) decoder_3 (
    .out4(decoder_3_out4), .out5(decoder_3_out5), .out6(decoder_3_out6), .out7(decoder_3_out7), .sel(opCode));  // open: out0, out1, out2, out3, out8, out9, out10, out11, out12, out13, out14, out15, en
  not not_3 (not_3_out, z);
  and and_8 (and_8_out, gt, decoder_3_out4, undriven_2);
  and and_9 (and_9_out, undriven_2, lt, decoder_3_out5);
  and and_10 (and_10_out, not_3_out, decoder_3_out6, undriven_3);
  and and_11 (and_11_out, undriven_3, z, decoder_3_out7);
  or or_3 (doJumpToImm, and_7_out, or_4_out);
  or or_4 (or_4_out, and_8_out, and_9_out, and_10_out, and_11_out);
endmodule

module REGIO (
  input  [7:0] PC,
  input  [15:0] rMemData,
  input  [15:0] aluRes,
  input  [15:0] HIReg,
  input  [15:0] LOReg,
  input  [15:0] _16imm,
  input  subOp,
  input  [3:0] opCode,
  output [15:0] wRegData
);

  wire decoder_1_out0, decoder_1_out1, decoder_1_out2, decoder_1_out10, not_1_out, undriven, useHI, useimm,
       useLO, useMEM, usePC;
  wire [7:0] adder_1_out;
  wire [15:0] bit_extender_1_out, multiplexer_1_out, multiplexer_2_out, multiplexer_3_out, multiplexer_4_out;

  Decoder #(.select(4)) decoder_1 (
    .out0(decoder_1_out0), .out1(decoder_1_out1), .out2(decoder_1_out2), .out10(decoder_1_out10), .sel(opCode));  // open: out3, out4, out5, out6, out7, out8, out9, out11, out12, out13, out14, out15, en
  not not_1 (not_1_out, subOp);
  and and_1 (useMEM, decoder_1_out0, subOp, undriven);
  and and_2 (usePC, undriven, not_1_out, decoder_1_out1);
  // AND_Gate and_3: pin names not known; wires that end beside it: not_1_out, useLO
  and and_4 (useHI, decoder_1_out10, decoder_1_out10, subOp);
  and and_5 (useimm, decoder_1_out2, subOp);
  Multiplexer #(.width(16)) multiplexer_1 (
    .in0(aluRes), .in1(HIReg), .out(multiplexer_1_out), .sel(useHI));  // open: en
  Multiplexer #(.width(16)) multiplexer_2 (
    .in0(multiplexer_1_out), .in1(LOReg), .out(multiplexer_2_out), .sel(useLO));  // open: en
  Multiplexer #(.width(16)) multiplexer_3 (
    .in0(multiplexer_2_out), .in1(rMemData), .out(multiplexer_3_out), .sel(useMEM));  // open: en
  Multiplexer #(.width(16)) multiplexer_4 (
    .in0(multiplexer_3_out), .in1(_16imm), .out(multiplexer_4_out), .sel(useimm));  // open: en
  Adder adder_1 (.a(PC), .b(8'h1), .out(adder_1_out));  // open: cin, cout
  assign bit_extender_1_out = {{8{1'b0}}, adder_1_out};  // Bit_Extender bit_extender_1
  Multiplexer #(.width(16)) multiplexer_5 (
    .in0(multiplexer_4_out), .in1(bit_extender_1_out), .out(wRegData), .sel(usePC));  // open: en
endmodule
