// Logisim project lab9B.circ as structural Verilog: 2 circuits, main circuit main
module main (
  input  [3:0] Number
);

  wire d0, d1, d2, d3, d4, d5, d6, d7;

  Solution solution (.Number_to_display(Number), .Segment_configuration({d7, d6, d5, d4, d3, d2, d1, d0}));
  _7_Segment_Display u_7_segment_display_1 (.g(d0), .f(d1), .a(d2), .b(d3), .e(d7), .d(d6), .c(d5), .dp(d4));

  // Notes on the sheet:
  //   This is what the autograder looks like
  //   1. Modify the solution subcircuit
  //   2. Make sure the circuit still connects correctly
  //   Change the number
  //   If you need to modify this circuit, your solution will fail!
  //   Display changes
endmodule

module Solution (
  input  [3:0] Number_to_display,
  output [7:0] Segment_configuration
);

  wire _1_0_out, _2_0_out, _2_1_p2, _2_10_out, _10_out, _20_out, n1_0_out, n2_0_out, n21_out, not_1_out,
       not_2_out, not_3_out, not_4_out, undriven, undriven_2, undriven_3, undriven_4, undriven_5;

  not not_1 (not_1_out, Number_to_display[3]);
  not not_2 (not_2_out, Number_to_display[2]);
  not not_3 (not_3_out, Number_to_display[1]);
  not not_4 (not_4_out, Number_to_display[0]);
  // AND_Gate _2_1: pin names not known; wires that end beside it: Number_to_display[2], _2_1_p2, not_3_out
  and _2_10 (_2_10_out, _2_1_p2, _2_1_p2, Number_to_display[0]);
  or _7 (Segment_configuration[7], _1_0_out, n2_0_out);
  or _6 (Segment_configuration[6], Number_to_display[3], n2_0_out, _2_10_out, n21_out, _1_0_out);
  or _5 (Segment_configuration[5], Number_to_display[0], not_3_out, Number_to_display[2]);
  and _2_0 (_2_0_out, Number_to_display[2], not_4_out, undriven);
  or _3 (Segment_configuration[3], not_2_out, n1_0_out, _10_out);
  and n21 (n21_out, undriven, not_2_out, Number_to_display[1]);
  or _2 (Segment_configuration[2], _20_out, Number_to_display[1], Number_to_display[3], n2_0_out);
  and _1_0 (_1_0_out, Number_to_display[1], not_4_out, undriven_2);
  and n1_0 (n1_0_out, undriven_2, not_3_out, not_4_out, undriven_3);
  and _10 (_10_out, undriven_3, Number_to_display[1], Number_to_display[0], undriven_4);
  and n2_0 (n2_0_out, undriven_4, not_2_out, not_4_out, undriven_5);
  or _1 (Segment_configuration[1], n1_0_out, _2_0_out, _2_1_p2, Number_to_display[3]);
  and _20 (_20_out, undriven_5, Number_to_display[2], Number_to_display[0]);
  or _0 (Segment_configuration[0], _1_0_out, n21_out, _2_1_p2, Number_to_display[3]);

  assign Segment_configuration[4] = 1'b0;

  // Other names for the same wires on the sheet: number[3:0] = Number_to_display;
  //   segments (some bits) = {Segment_configuration[7:5], Segment_configuration[3:0]}

  // Notes on the sheet:
  //   These are the inputs
  //   of your circuit.
  //   Do not modify this!
  //   Shane Riley -- spr33
  //   These are the outputs
  //   of your circuit.
  //   Do not modify this!
endmodule
